# Fritzing sketch esp (saved by Fritzing 0.9.3b)
breadboards: 1

parts:
  U1 = ESP8266 WiFi Module [part_number=ESP8266]
  R1 = Rotary Potentiometer (Large) [maximum_resistance=100kΩ package=THT]

nets:
  N1: U1.3.3V#10, R1.leg1
  N2: U1.GND#13, R1.leg2
  N3: U1.IO13, R1.wiper
