# Fritzing sketch smart garage (saved by Fritzing 0.9.3b)
breadboards: 1

parts:
  Componente1 = Arduino Uno (Rev3)
  hc-sr1 = hc-sr04
  LED1 = LED - 5mm [color="Green (555nm)" package="5 mm [THT]"]
  LED2 = LED - 5mm [color="Green (555nm)" package="5 mm [THT]"]
  LED3 = LED - 5mm [color="Red (633nm)" package="5 mm [THT]"]
  R1 = Resistor [tolerance=±5% resistance=220 package=THT]
  R2 = Resistor [tolerance=±5% resistance=220 package=THT]
  R3 = Resistor [tolerance=±5% resistance=220 package=THT]
  R4 = Resistor [tolerance=±5% resistance=10k package=THT]
  R5 = Resistor [tolerance=±5% resistance=1k package=THT]
  S1 = Pushbutton [package="[THT]"]
  S2 = Pushbutton [package="[THT]"]
  PIR1 = PIR sensor

nets:
  N1: Componente1.D8, hc-sr1.Trig
  N2: Componente1.D11_PWM/MOSI, R1.Pin_1
  N3: Componente1.D2, R4.Pin_1, S1.Pin_3, S1.Pin_4
  N4: Componente1.D3_PWM, R5.Pin_1, S2.Pin_3, S2.Pin_4
  N5: Componente1.D4, PIR1.SIG
  N6: Componente1.D5_PWM, R3.Pin_1
  N7: Componente1.D6_PWM, R2.Pin_1
  N8: Componente1.D7, hc-sr1.Echo
  5V: Componente1.5V, hc-sr1.VCC, S1.Pin_1, S1.Pin_2, S2.Pin_1, S2.Pin_2, PIR1.VDD
  GND: Componente1.GND, hc-sr1.GND, LED1.cathode, LED2.cathode, LED3.cathode, PIR1.GND
  N9: LED1.anode, R1.Pin_0
  N10: LED2.anode, R2.Pin_0
  N11: LED3.anode, R3.Pin_0
