# Fritzing sketch smart_door_fr (saved by Fritzing 0.9.3b)
breadboards: 1

parts:
  Componente1 = Arduino Uno (Rev3) - ICSP
  LED1 = LED - 5mm [color="Green (555nm)" package="5 mm [THT]"]
  R1 = Resistor [tolerance=±5% resistance=220 package="0805 [SMD]"]
  R2 = Resistor [tolerance=±5% resistance=220 package="0805 [SMD]"]
  LED2 = LED - 5mm [color="Red (633nm)" package="5 mm [THT]"]
  S1 = Pushbutton [package="[THT]"]
  R3 = Resistor [tolerance=±5% resistance=220 package="0805 [SMD]"]
  PIR1 = PIR sensor
  hc-sr1 = hc-sr04
  J1 = Basic Servo
  LED3 = LED - 5mm [color="Green (555nm)" package="5 mm [THT]"]
  R4 = Resistor [tolerance=±5% resistance=220 package="0805 [SMD]"]
  LED4 = LED - 5mm [color="Red (633nm)" package="5 mm [THT]"]
  R5 = Resistor [tolerance=±5% resistance=220 package="0805 [SMD]"]
  Componente2 = Bluetooth HC-05 Macho  # not connected
  Raspberry_Pi1 = Raspberry Pi 2
  T1 = TMP36 Temperature Sensor [package="TO92 [THT]"]

nets:
  N1: Componente1.A5/SCL, T1.Vout
  N2: Componente1.D8, hc-sr1.Trig
  N3: Componente1.D11_PWM/MOSI, S1.Pin_1, S1.Pin_2, R3.Pin_1
  N4: Componente1.D12/MISO, R4.Pin_0
  N5: Componente1.D4, PIR1.SIG
  N6: Componente1.D5_PWM, J1.pulse
  N7: Componente1.D6_PWM, R5.Pin_1
  N8: Componente1.D7, hc-sr1.Echo
  GND: Componente1.GND, LED1.cathode, LED2.cathode, R3.Pin_0, PIR1.GND, hc-sr1.GND, J1.gnd, LED3.cathode, LED4.cathode, T1.GND
  N9: LED1.anode, R2.Pin_0
  N10: R1.Pin_0, LED2.anode
  N11: R1.Pin_1, Raspberry_Pi1.GPIO27
  N12: R2.Pin_1, Raspberry_Pi1.GPIO17
  VCC: S1.Pin_3, S1.Pin_4, PIR1.VDD, hc-sr1.VCC, J1.vcc, T1.+Vs
  N13: LED3.anode, R4.Pin_1
  N14: LED4.anode, R5.Pin_0

custom parts:
  Arduino Uno (Rev3) - ICSP: The Arduino Uno is a microcontroller board based on the ATmega328 (datasheet). It has 14 digital input/output pins (of which 6 can be used as PWM outputs), 6 analog inputs, a 16 MHz ceramic resonator, a USB connection, a power jack, an ICSP header, and a reset button. It contains everything needed to support the microcontroller; simply connect it to a computer with a USB cable or power it with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
